# Fritzing sketch water_heater (saved by Fritzing 0.9.3b)
breadboards: 1

parts:
  Part1 = Arduino Nano (Rev3.0)
  U1 = RELAY [package=relay-jzc]
  U2 = RELAY [package=relay-jzc]
  Part2 = NRF24L01+ Breakout Board
  LED3 = smd LED [color="White (4500K)" package="0603 [SMD]"]
  C1 = Electrolytic Capacitor [capacitance=47µF package="100 mil [THT, electrolytic]"]
  HLK-PM1 = HLK-PM01
  U3 = RELAY [package=relay-jzc]
  TTP223B2 = TTP223B Capacitive Touch Sensor Module
  TTP223B3 = TTP223B Capacitive Touch Sensor Module
  TTP223B4 = TTP223B Capacitive Touch Sensor Module

nets:
  N1: Part1.RESET, Part1.A0
  GND: Part1.GND, Part2.GND, LED3.cathode, C1.-, HLK-PM1.-Vo, TTP223B2.GND, TTP223B3.GND, TTP223B4.GND
  N2: Part1.D2, TTP223B2.SIG
  N3: Part1.D3, TTP223B3.SIG
  N4: Part1.D4, U1.NC
  N5: Part1.D5, U2.NC
  N6: Part1.D6, U3.NC
  N7: Part1.D9, Part2.CE
  N8: Part1.D10, Part2.CS
  N9: Part1.D11/MOSI, Part2.MOSI
  N10: Part1.D12/MISO, Part2.MISO
  VCC: Part1.5V, Part2.VCC, C1.+, HLK-PM1.+Vo, TTP223B2.VCC, TTP223B3.VCC, TTP223B4.VCC
  N11: Part1.A3, TTP223B4.SIG
  N12: Part1.A2, LED3.anode
  N13: Part1.D13/SCK, Part2.SCK

notes:
  A0 it OTA reset

custom parts:
  TTP223B Capacitive Touch Sensor Module: The TTP223B capacitive touch sensor module uses the TTP223B IC. The appropriate voltage is approximately 2 to 5.5 volts.

// code stored in the sketch: shade_station.ino
#include "common.h"

#define SHADE_UP 6
#define SHADE_DOWN 7
#define MY_HIGH LOW
#define MY_LOW HIGH

unsigned long startTime = millis();
unsigned long currentTime = millis();
bool inAction = false;
void configureEEPROMAddressForRFAndOTA(void)
{
  //my address "003"
  EEPROM.write(0, 48);
  EEPROM.write(1, 48);
  EEPROM.write(2, 51);

  //OTA station address (always "000")
  EEPROM.write(3, 48);
  EEPROM.write(4, 48);
  EEPROM.write(5, 48);
}
void setup()
{

  Serial.begin(115200);
  Serial.println("setup...");
  configureEEPROMAddressForRFAndOTA();
  pinMode(SHADE_UP, OUTPUT);
  pinMode(SHADE_DOWN, OUTPUT);
  stop();
  startRF();
}

void stop(void)
{
  inAction = false;
  digitalWrite(SHADE_UP, MY_HIGH);
  digitalWrite(SHADE_DOWN, MY_HIGH);
  Serial.println("Stop...");
  delay(1000);
}

void down(void)
{
  stop();
  startTime = millis();
  inAction = true;
  digitalWrite(SHADE_DOWN, MY_LOW);
  Serial.println("Down...");
}

void up(void)
{
  stop();
  startTime = millis();
  inAction = true;
  digitalWrite(SHADE_UP, MY_LOW);
  Serial.println("Up...");
}

void stopNeeded(void)
{
  if (!inAction)
  {
    return;
  }
  currentTime = millis();
  unsigned long elapsedTime = currentTime - startTime;
  Serial.print("elapsedTime: ");
  Serial.println(elapsedTime);
  if (elapsedTime > 38000)
  {
    Serial.println("timeup stopping..");
    stop();
  }
}

void loop()
{
  stopNeeded();
  Serial.println("Listening...");
  while (!Mirf.dataReady())
  {
    //Serial.println("rest...");
    //stopNeeded();
    watchdogReset();
    delay(100);
  };

  Serial.println("Data...");

  char cmd[Mirf.payload + 1];
  checkIfOtaRequestOrLoadCommand(cmd);
  Serial.print("Return data: ");
  Serial.println(cmd);
  if (strcmp(cmd, "000") == 0)
  {
    stop();
  }
  else if (strcmp(cmd, "001") == 0)
  {
    up();
  }
  else if (strcmp(cmd, "002") == 0)
  {
    down();
  }
  else if (strcmp(cmd, "003") == 0)
  {
    while (1)
    {
      soft_restart();
    }
  }

  watchdogReset();
}

// code stored in the sketch: shade_station_2.ino
#include "common.h"

#define SHADE_UP 6
#define SHADE_DOWN 7

#define LED_PIN 5
#define LED2_PIN 8

#define MY_HIGH LOW
#define MY_LOW HIGH

unsigned long startTime = millis();
unsigned long currentTime = millis();
bool inAction = false;
void configureEEPROMAddressForRFAndOTA(void)
{
  //my address "003"
  EEPROM.write(0, 48);
  EEPROM.write(1, 48);
  EEPROM.write(2, 50);

  //OTA station address (always "000")
  EEPROM.write(3, 48);
  EEPROM.write(4, 48);
  EEPROM.write(5, 48);
}
void setup()
{

  Serial.begin(115200);
  Serial.println("setup...");
  configureEEPROMAddressForRFAndOTA();
  pinMode(SHADE_UP, OUTPUT);
  pinMode(SHADE_DOWN, OUTPUT);
  pinMode(LED_PIN, OUTPUT);
  stop();
  startRF();
}

void stop(void)
{
  inAction = false;
  digitalWrite(SHADE_UP, MY_HIGH);
  digitalWrite(SHADE_DOWN, MY_HIGH);
  Serial.println("Stop...");
  delay(1000);
}

void down(void)
{
  stop();
  startTime = millis();
  inAction = true;
  digitalWrite(SHADE_DOWN, MY_LOW);
  Serial.println("Down...");
}

void up(void)
{
  stop();
  startTime = millis();
  inAction = true;
  digitalWrite(SHADE_UP, MY_LOW);
  Serial.println("Up...");
}

void stopNeeded(void)
{
  if (!inAction)
  {
    return;
  }
  currentTime = millis();
  unsigned long elapsedTime = currentTime - startTime;
  Serial.print("elapsedTime: ");
  Serial.println(elapsedTime);
  if (elapsedTime > 38000)
  {
    Serial.println("timeup stopping..");
    stop();
  }
}

void blink(int d)
{
  digitalWrite(LED_PIN, HIGH);
  delay(d/2);
  digitalWrite(LED_PIN, LOW);
  delay(d/2);
}

void blink2(int d)
{
  digitalWrite(LED2_PIN, HIGH);
  delay(d);
  digitalWrite(LED2_PIN, LOW);
}
void loop()
{
  blink(500);
  blink(500);
  //stopNeeded();
  Serial.println("Listening...");
  while (!Mirf.dataReady())
  {
    //stopNeeded();
    watchdogReset();
    blink(100);
  };

  Serial.println("Data...");

  blink2(500);
  char cmd[Mirf.payload + 1];
  checkIfOtaRequestOrLoadCommand(cmd);
  Serial.print("Return data: ");
  Serial.println(cmd);
  if (strcmp(cmd, "000") == 0)
  {
    stop();
  }
  else if (strcmp(cmd, "001") == 0)
  {
    up();
  }
  else if (strcmp(cmd, "002") == 0)
  {
    down();
  }
  else if (strcmp(cmd, "003") == 0)
  {
//    while (1)
//    {
//      soft_restart();
//    }
  }
  while( Mirf.isSending() ) ; 
}
