# Fritzing sketch BT_To_Ant_Dispatch_Station_model (saved by Fritzing 0.9.3b)
circuit board: 8.46667cm x 5.64444cm
breadboards: 1

parts:
  BT = Bluetooth HC-05 Macho
  Nano = Arduino Nano (Rev3.0)
  RF = NRF24L01+ Breakout Board

nets:
  N1: BT.TXD, Nano.D6
  N2: BT.RXD, Nano.D7
  VCC: BT.VCC, Nano.5V, RF.VCC
  GND: BT.GND, Nano.GND, RF.GND
  N3: Nano.D10, RF.CS
  N4: Nano.D11/MOSI, RF.MOSI
  N5: Nano.D12/MISO, RF.MISO
  N6: Nano.D13/SCK, RF.SCK

// code stored in the sketch: BT_To_Ant_Dispatch_Station.ino

#include <SoftwareSerial.h>
#include <SPI.h>
#include <Mirf.h>
#include <nRF24L01.h>
#include <MirfHardwareSpiDriver.h>

const int Radio_CSN = 10; // pinnenummer brukt for CSN på radio (ikke endre denne)
const int Radio_CE  = 9;  //


SoftwareSerial BTSerial(6, 7); // RX | TX

// Structure of our payload
//struct payload_t
//{
//  unsigned long main_command;//1 ac
//  unsigned long sub_command;//1=on, 0=off
//};

void setup()
{

  Serial.begin(9600);
  Serial.println("Dispatch station ready.");
  //BTSerial.begin(38400);  // HC-05 default speed in AT command more
  BTSerial.begin(9600);  //custom
  SPI.begin();
  /*
    Set the SPI Driver.
  */
  Mirf.csnPin =  Radio_CSN;
  Mirf.spi = &MirfHardwareSpi;
  /*
     Setup pins / SPI.
  */
  Mirf.init();
  /*
     Configure reciving address.
  */
  Mirf.setRADDR((byte *)"serv1");
  /*
     Set the payload length to sizeof(unsigned long) the
     return type of millis().

     NB: payload on client and server must be the same.
  */
  Mirf.payload = sizeof(unsigned long);
  /*
     Write channel and payload config then power up reciver.
  */
  Mirf.config();
}

int i = 0;
void loop()
{

  digitalWrite(Radio_CSN, LOW); // ENABLE radio

  // Keep reading from HC-05 and send to Arduino Serial Monitor
  if (BTSerial.available())
  {
    char command = BTSerial.read();
    Serial.println(command);
    delay(1000);
    //add code to check what was requested from serial server (PI station)
    byte data[Mirf.payload];
    if (!Mirf.isSending() /*&& Mirf.dataReady()*/) {
      Mirf.setTADDR((byte *)"irir1");
      Serial.println("sending packet");
      if (command == '1')
      {
        Serial.println("command 1");
        data[0] = 1;
        data[1] = 1;
        Mirf.send(data);
      }
      else if (command == '2')
      {
        Serial.println("command 2");
        data[0] = 1;
        data[1] = 0;
        Mirf.send(data);
      }
    }
  }
}
