# Fritzing sketch shade_station (saved by Fritzing 0.9.3b)
breadboards: 1

parts:
  Part1 = Arduino Nano (Rev3.0)
  U1 = RELAY [package=relay-jzc]
  U2 = RELAY [package=relay-jzc]
  Part2 = NRF24L01+ Breakout Board
  LED2 = smd LED [color="Red (633nm)" package="0603 [SMD]"]
  LED3 = smd LED [color="White (4500K)" package="0603 [SMD]"]
  C1 = Electrolytic Capacitor [capacitance=47µF package="100 mil [THT, electrolytic]"]
  U3 = RELAY-SOLIDSTATE [package=relay-s108t02]  # not connected
  U4 = RELAY-SOLIDSTATE [package=relay-s108t02]  # not connected
  HLK-PM1 = HLK-PM01

nets:
  GND: Part1.GND, Part2.GND, LED2.cathode, LED3.cathode, C1.-, HLK-PM1.-Vo
  N1: Part1.D5, LED2.anode
  N2: Part1.D6, U1.NC
  N3: Part1.D7, U2.NC
  N4: Part1.D8, LED3.anode
  N5: Part1.D9, Part2.CE
  N6: Part1.D10, Part2.CS
  N7: Part1.D11/MOSI, Part2.MOSI
  N8: Part1.D12/MISO, Part2.MISO
  N9: Part1.5V, HLK-PM1.+Vo
  3V3: Part1.3V3, Part2.VCC, C1.+
  N10: Part1.D13/SCK, Part2.SCK

// code stored in the sketch: shade_station.ino
#include "common.h"

#define SHADE_UP 6
#define SHADE_DOWN 7
#define MY_HIGH LOW
#define MY_LOW HIGH

unsigned long startTime = millis();
unsigned long currentTime = millis();
bool inAction = false;
void configureEEPROMAddressForRFAndOTA(void)
{
  //my address "003"
  EEPROM.write(0, 48);
  EEPROM.write(1, 48);
  EEPROM.write(2, 51);

  //OTA station address (always "000")
  EEPROM.write(3, 48);
  EEPROM.write(4, 48);
  EEPROM.write(5, 48);
}
void setup()
{

  Serial.begin(115200);
  Serial.println("setup...");
  configureEEPROMAddressForRFAndOTA();
  pinMode(SHADE_UP, OUTPUT);
  pinMode(SHADE_DOWN, OUTPUT);
  stop();
  startRF();
}

void stop(void)
{
  inAction = false;
  digitalWrite(SHADE_UP, MY_HIGH);
  digitalWrite(SHADE_DOWN, MY_HIGH);
  Serial.println("Stop...");
  delay(1000);
}

void down(void)
{
  stop();
  startTime = millis();
  inAction = true;
  digitalWrite(SHADE_DOWN, MY_LOW);
  Serial.println("Down...");
}

void up(void)
{
  stop();
  startTime = millis();
  inAction = true;
  digitalWrite(SHADE_UP, MY_LOW);
  Serial.println("Up...");
}

void stopNeeded(void)
{
  if (!inAction)
  {
    return;
  }
  currentTime = millis();
  unsigned long elapsedTime = currentTime - startTime;
  Serial.print("elapsedTime: ");
  Serial.println(elapsedTime);
  if (elapsedTime > 38000)
  {
    Serial.println("timeup stopping..");
    stop();
  }
}

void loop()
{
  stopNeeded();
  Serial.println("Listening...");
  while (!Mirf.dataReady())
  {
    //Serial.println("rest...");
    //stopNeeded();
    watchdogReset();
    delay(100);
  };

  Serial.println("Data...");

  char cmd[Mirf.payload + 1];
  checkIfOtaRequestOrLoadCommand(cmd);
  Serial.print("Return data: ");
  Serial.println(cmd);
  if (strcmp(cmd, "000") == 0)
  {
    stop();
  }
  else if (strcmp(cmd, "001") == 0)
  {
    up();
  }
  else if (strcmp(cmd, "002") == 0)
  {
    down();
  }
  else if (strcmp(cmd, "003") == 0)
  {
    while (1)
    {
      soft_restart();
    }
  }

  watchdogReset();
}

// code stored in the sketch: shade_station_2.ino
#include "common.h"

#define SHADE_UP 6
#define SHADE_DOWN 7

#define LED_PIN 5
#define LED2_PIN 8

#define MY_HIGH LOW
#define MY_LOW HIGH

unsigned long startTime = millis();
unsigned long currentTime = millis();
bool inAction = false;
void configureEEPROMAddressForRFAndOTA(void)
{
  //my address "003"
  EEPROM.write(0, 48);
  EEPROM.write(1, 48);
  EEPROM.write(2, 50);

  //OTA station address (always "000")
  EEPROM.write(3, 48);
  EEPROM.write(4, 48);
  EEPROM.write(5, 48);
}
void setup()
{

  Serial.begin(115200);
  Serial.println("setup...");
  configureEEPROMAddressForRFAndOTA();
  pinMode(SHADE_UP, OUTPUT);
  pinMode(SHADE_DOWN, OUTPUT);
  pinMode(LED_PIN, OUTPUT);
  stop();
  startRF();
}

void stop(void)
{
  inAction = false;
  digitalWrite(SHADE_UP, MY_HIGH);
  digitalWrite(SHADE_DOWN, MY_HIGH);
  Serial.println("Stop...");
  delay(1000);
}

void down(void)
{
  stop();
  startTime = millis();
  inAction = true;
  digitalWrite(SHADE_DOWN, MY_LOW);
  Serial.println("Down...");
}

void up(void)
{
  stop();
  startTime = millis();
  inAction = true;
  digitalWrite(SHADE_UP, MY_LOW);
  Serial.println("Up...");
}

void stopNeeded(void)
{
  if (!inAction)
  {
    return;
  }
  currentTime = millis();
  unsigned long elapsedTime = currentTime - startTime;
  Serial.print("elapsedTime: ");
  Serial.println(elapsedTime);
  if (elapsedTime > 38000)
  {
    Serial.println("timeup stopping..");
    stop();
  }
}

void blink(int d)
{
  digitalWrite(LED_PIN, HIGH);
  delay(d/2);
  digitalWrite(LED_PIN, LOW);
  delay(d/2);
}

void blink2(int d)
{
  digitalWrite(LED2_PIN, HIGH);
  delay(d);
  digitalWrite(LED2_PIN, LOW);
}
void loop()
{
  blink(500);
  blink(500);
  //stopNeeded();
  Serial.println("Listening...");
  while (!Mirf.dataReady())
  {
    //stopNeeded();
    watchdogReset();
    blink(100);
  };

  Serial.println("Data...");

  blink2(500);
  char cmd[Mirf.payload + 1];
  checkIfOtaRequestOrLoadCommand(cmd);
  Serial.print("Return data: ");
  Serial.println(cmd);
  if (strcmp(cmd, "000") == 0)
  {
    stop();
  }
  else if (strcmp(cmd, "001") == 0)
  {
    up();
  }
  else if (strcmp(cmd, "002") == 0)
  {
    down();
  }
  else if (strcmp(cmd, "003") == 0)
  {
//    while (1)
//    {
//      soft_restart();
//    }
  }
  while( Mirf.isSending() ) ; 
}
